// Logisim project tree_multiplier_4bit.circ as structural Verilog: 3 circuits, main circuit main
module main (
  input  [3:0] Mlp,
  input  [3:0] Mol,
  output [7:0] out_3
);

  wire alu4_1_carry_out, alu5_1_carry_out;
  wire [0:0] bit_extender_3_out;
  wire [3:0] alu4_1_r, alu4_2_r, and_1_out, and_2_out, and_3_out, and_4_out, bit_extender_1_out,
       bit_extender_2_out, bit_extender_3_out_2, bit_extender_4_out, bit_extender_5_out, bit_extender_6_out;

  assign bit_extender_1_out = {{3{Mol[3]}}, Mol[3]};  // Bit_Extender bit_extender_1
  // Probe on and_1_out
  assign and_1_out = bit_extender_1_out & Mlp;  // AND_Gate and_1, 4 bits wide
  alu4 alu4_1 (.A(and_1_out), .B(bit_extender_3_out_2), .R(alu4_1_r), .Carry_out(alu4_1_carry_out));  // open: Carry_In
  // Probe on alu4_1_r
  assign bit_extender_2_out = {{3{Mol[2]}}, Mol[2]};  // Bit_Extender bit_extender_2
  assign and_2_out = bit_extender_2_out & Mlp;  // AND_Gate and_2, 4 bits wide
  // Probe on and_2_out
  xor xor_1 (out_3[7], alu4_1_carry_out, alu5_1_carry_out);
  assign {bit_extender_3_out_2, bit_extender_3_out[0]} = {{1{1'b0}}, and_2_out};  // Bit_Extender bit_extender_3
  // Probe on {alu4_1_r, bit_extender_3_out[0]}
  alu5 alu5_1 (
    .A({alu4_1_r, bit_extender_3_out[0]}), .B({1'b0, alu4_2_r}), .R(out_3[6:2]), .Carry_out(alu5_1_carry_out));  // open: Carry_In
  // Probe on out_3[6:2]
  assign bit_extender_4_out = {{3{Mol[1]}}, Mol[1]};  // Bit_Extender bit_extender_4
  assign and_3_out = bit_extender_4_out & Mlp;  // AND_Gate and_3, 4 bits wide
  // Probe on and_3_out
  // Probe on {1'b0, alu4_2_r}
  alu4 alu4_2 (
    .A(and_3_out), .B(bit_extender_6_out), .R({alu4_2_r[2:0], out_3[1]}), .Carry_out(alu4_2_r[3]));  // open: Carry_In
  // Probe on {alu4_2_r[2:0], out_3[1]}
  assign bit_extender_5_out = {{3{Mol[0]}}, Mol[0]};  // Bit_Extender bit_extender_5
  assign and_4_out = bit_extender_5_out & Mlp;  // AND_Gate and_4, 4 bits wide
  // Probe on and_4_out
  assign {bit_extender_6_out, out_3[0]} = {{1{1'b0}}, and_4_out};  // Bit_Extender bit_extender_6
endmodule

module alu4 (
  input  [3:0] A,
  input  Carry_In,
  input  [3:0] B,
  output [3:0] R,
  output Carry_out
);

  Adder #(.width(4)) adder_1 (.a(A), .b(B), .out(R), .cin(Carry_In), .cout(Carry_out));
endmodule

module alu5 (
  input  [4:0] A,
  input  Carry_In,
  input  [4:0] B,
  output [4:0] R,
  output Carry_out
);

  Adder #(.width(5)) adder_1 (.a(A), .b(B), .out(R), .cin(Carry_In), .cout(Carry_out));
endmodule
